# Fritzing sketch schematic-fritzing (saved by Fritzing 0.9.3b)
breadboards: 1

parts:
  M1 = BME280  # not connected
  M2 = BME280
  U1 = ESP32S-HiLetgo [part_number=ESP32S-HiLetgo]
  Componente1 = SRF05 Ultrasonic Rangefinder

nets:
  N1: M2.VIN, U1.3.3
  GND: M2.GND, U1.GND, Componente1.GND
  N2: M2.SCL, U1.GPIO22
  N3: M2.SDA, U1.GPIO21
  VIN: U1.VIN, Componente1.VCC
  N4: U1.GPIO16, Componente1.Echo
  N5: U1.GPIO17, Componente1.Trig

custom parts:
  BME280: Temperature Humidity Barometric presure Sensor
  ESP32S-HiLetgo: HiLetgo ESP-WROOM-32 ESP32 ESP-32S Development Board 2.4GHz Dual-Mode WiFi + Bluetooth Dual Cores Microcontroller The ESP32 integrated with Antenna switches, RF Balun, power amplifiers, low-noise amplifiers, filters, and management modules, and the entire solution occupies the least area of PCB. 2.4 GHz Wi-Fi plus Bluetooth dual-mode chip, with TSMC Ultra-low power consumption 40nm technology,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
